// Logisim project 8bitCPU.circ as structural Verilog
module CPU_MEM_1 (
  input  s,
  input  e,
  output q
);

  wire nand_1_out, nand_2_out, nand_4_out;

  nand nand_1 (nand_1_out, s, e);
  nand nand_2 (nand_2_out, nand_1_out, e);
  nand nand_3 (q, nand_1_out, nand_4_out);
  nand nand_4 (nand_4_out, q, nand_2_out);
endmodule

module CPU_MEM_8 (
  input  [7:0] I,
  input  S,
  output [7:0] O
);

  CPU_MEM_1 cpu_mem_1_1 (.s(I[0]), .e(S), .q(O[0]));
  CPU_MEM_1 cpu_mem_1_2 (.s(I[1]), .e(S), .q(O[1]));
  CPU_MEM_1 cpu_mem_1_3 (.s(I[2]), .e(S), .q(O[2]));
  CPU_MEM_1 cpu_mem_1_4 (.s(I[3]), .e(S), .q(O[3]));
  CPU_MEM_1 cpu_mem_1_5 (.s(I[4]), .e(S), .q(O[4]));
  CPU_MEM_1 cpu_mem_1_6 (.s(I[5]), .e(S), .q(O[5]));
  CPU_MEM_1 cpu_mem_1_7 (.s(I[6]), .e(S), .q(O[6]));
  CPU_MEM_1 cpu_mem_1_8 (.s(I[7]), .e(S), .q(O[7]));
endmodule

module CPU_ENABLE_8 (
  input  [7:0] I,
  input  E,
  output [7:0] O
);

  and and_1 (O[0], I[0], E);
  and and_2 (O[1], I[1], E);
  and and_3 (O[2], I[2], E);
  and and_4 (O[3], I[3], E);
  and and_5 (O[4], I[4], E);
  and and_6 (O[5], I[5], E);
  and and_7 (O[6], I[6], E);
  and and_8 (O[7], I[7], E);
endmodule

module CPU_REG_8 (
  input  [7:0] I,
  input  E,
  input  S,
  output [7:0] R,
  output [7:0] O
);

  CPU_MEM_8 cpu_mem_8_1 (.I(I), .S(S), .O(R));
  CPU_ENABLE_8 cpu_enable_8_1 (.I(R), .E(E), .O(O));
endmodule

module CPU_ADDER (
  input  a,
  input  b,
  input  carry_in,
  output carry_out,
  output sum
);

  wire and_1_out, and_2_out, xor_1_out;

  xor xor_1 (xor_1_out, a, b);
  and and_1 (and_1_out, carry_in, xor_1_out);
  and and_2 (and_2_out, a, b);
  xor xor_2 (carry_out, xor_1_out, carry_in);
  or or_1 (sum, and_1_out, and_2_out);
endmodule

module SHR (
  input  Shift_In,
  input  [7:0] I,
  output Shift_Out,
  output [7:0] O
);

  wire [7:1] cpu_reg_8_1_r;

  CPU_REG_8 cpu_reg_8_1 (.I(I), .E(1'b1), .S(1'b1), .R({cpu_reg_8_1_r, Shift_Out}));  // open: O
  CPU_REG_8 cpu_reg_8_2 (.I({Shift_In, cpu_reg_8_1_r}), .E(1'b1), .S(1'b1), .R(O));  // open: O
endmodule

module SHL (
  input  Shift_In,
  input  [7:0] I,
  output [7:0] O,
  output Shift_Out
);

  wire [6:0] cpu_reg_8_1_r;

  CPU_REG_8 cpu_reg_8_1 (.I(I), .E(1'b1), .S(1'b1), .R({Shift_Out, cpu_reg_8_1_r}));  // open: O
  CPU_REG_8 cpu_reg_8_2 (.I({cpu_reg_8_1_r, Shift_In}), .E(1'b1), .S(1'b1), .R(O));  // open: O
endmodule

module NOT_8 (
  input  [7:0] I,
  output [7:0] O
);

  not not_1 (O[0], I[0]);
  not not_2 (O[1], I[1]);
  not not_3 (O[2], I[2]);
  not not_4 (O[3], I[3]);
  not not_5 (O[4], I[4]);
  not not_6 (O[5], I[5]);
  not not_7 (O[6], I[6]);
  not not_8 (O[7], I[7]);
endmodule

module AND_8 (
  input  [7:0] A,
  input  [7:0] B,
  output [7:0] O
);

  and and_1 (O[0], A[0], B[0]);
  and and_2 (O[1], A[1], B[1]);
  and and_3 (O[2], A[2], B[2]);
  and and_4 (O[3], A[3], B[3]);
  and and_5 (O[4], A[4], B[4]);
  and and_6 (O[5], A[5], B[5]);
  and and_7 (O[6], A[6], B[6]);
  and and_8 (O[7], A[7], B[7]);
endmodule

module OR_8 (
  input  [7:0] A,
  input  [7:0] B,
  output [7:0] O
);

  or or_1 (O[0], A[0], B[0]);
  or or_2 (O[1], A[1], B[1]);
  or or_3 (O[2], A[2], B[2]);
  or or_4 (O[3], A[3], B[3]);
  or or_5 (O[4], A[4], B[4]);
  or or_6 (O[5], A[5], B[5]);
  or or_7 (O[6], A[6], B[6]);
  or or_8 (O[7], A[7], B[7]);
endmodule

module XOR_1 (
  input  larger,
  input  above_equal,
  input  a,
  input  b,
  output q,
  output equal,
  output a_large
);

  wire and_2_out, not_1_out;

  xor xor_1 (q, a, b);
  not not_1 (not_1_out, q);
  and and_1 (equal, not_1_out, above_equal);
  and and_2 (and_2_out, above_equal, a, q);
  or or_1 (a_large, and_2_out, larger);
endmodule

module XOR_8 (
  input  [7:0] A,
  input  [7:0] B,
  output [7:0] O,
  output larger,
  output equal
);

  wire xor_1_1_a_large, xor_1_1_equal, xor_1_2_a_large, xor_1_2_equal, xor_1_3_a_large, xor_1_3_equal,
       xor_1_4_a_large, xor_1_4_equal, xor_1_5_a_large, xor_1_5_equal, xor_1_6_a_large, xor_1_6_equal,
       xor_1_7_a_large, xor_1_7_equal;

  XOR_1 xor_1_1 (
    .larger(1'b0), .above_equal(1'b1), .a(A[0]), .b(B[0]), .q(O[0]), .equal(xor_1_1_equal),
    .a_large(xor_1_1_a_large));
  XOR_1 xor_1_2 (
    .larger(xor_1_1_a_large), .above_equal(xor_1_1_equal), .a(A[1]), .b(B[1]), .q(O[1]),
    .equal(xor_1_2_equal), .a_large(xor_1_2_a_large));
  XOR_1 xor_1_3 (
    .larger(xor_1_2_a_large), .above_equal(xor_1_2_equal), .a(A[2]), .b(B[2]), .q(O[2]),
    .equal(xor_1_3_equal), .a_large(xor_1_3_a_large));
  XOR_1 xor_1_4 (
    .larger(xor_1_3_a_large), .above_equal(xor_1_3_equal), .a(A[3]), .b(B[3]), .q(O[3]),
    .equal(xor_1_4_equal), .a_large(xor_1_4_a_large));
  XOR_1 xor_1_5 (
    .larger(xor_1_4_a_large), .above_equal(xor_1_4_equal), .a(A[4]), .b(B[4]), .q(O[4]),
    .equal(xor_1_5_equal), .a_large(xor_1_5_a_large));
  XOR_1 xor_1_6 (
    .larger(xor_1_5_a_large), .above_equal(xor_1_5_equal), .a(A[5]), .b(B[5]), .q(O[5]),
    .equal(xor_1_6_equal), .a_large(xor_1_6_a_large));
  XOR_1 xor_1_7 (
    .larger(xor_1_6_a_large), .above_equal(xor_1_6_equal), .a(A[6]), .b(B[6]), .q(O[6]),
    .equal(xor_1_7_equal), .a_large(xor_1_7_a_large));
  XOR_1 xor_1_8 (
    .larger(xor_1_7_a_large), .above_equal(xor_1_7_equal), .a(A[7]), .b(B[7]), .q(O[7]), .equal(equal),
    .a_large(larger));
endmodule

module CPU_Z (
  input  [7:0] I,
  output O
);

  or or_1 (O, I[0], I[1], I[2], I[3], I[4], I[5], I[6], I[7]);
endmodule

module CPU_ALU (
  input  [7:0] A,
  input  carry_in,
  input  [7:0] B,
  input  in_4,
  input  in_5,
  input  in_6,
  output a_larger,
  output equal,
  output zero,
  output [7:0] O,
  output Carry_Out
);

  wire cpu_adder_8_1_carry_out, shl_1_shift_out, shr_1_shift_out;
  wire [7:0] and_8_1_o, cpu_adder_8_1_o, decoder_3x8_1_o, not_8_1_o, or_8_1_o, shl_1_o, shr_1_o, xor_8_1_o;

  NOT_8 not_8_1 (.I(A), .O(not_8_1_o));
  XOR_8 xor_8_1 (.A(A), .B(B), .O(xor_8_1_o), .larger(a_larger), .equal(equal));
  OR_8 or_8_1 (.A(A), .B(B), .O(or_8_1_o));
  AND_8 and_8_1 (.A(A), .B(B), .O(and_8_1_o));
  SHL shl_1 (.Shift_In(carry_in), .I(A), .O(shl_1_o), .Shift_Out(shl_1_shift_out));
  SHR shr_1 (.Shift_In(carry_in), .I(B), .Shift_Out(shr_1_shift_out), .O(shr_1_o));
  and and_1 (Carry_Out, shr_1_shift_out, decoder_3x8_1_o[6]);
  CPU_ADDER_8 cpu_adder_8_1 (
    .A(A), .carry_in(carry_in), .B(B), .carry_out(cpu_adder_8_1_carry_out), .O(cpu_adder_8_1_o));
  and and_2 (Carry_Out, cpu_adder_8_1_carry_out, decoder_3x8_1_o[1]);
  Decoder_3x8 decoder_3x8_1 (.A(in_4), .B(in_5), .C(in_6), .O(decoder_3x8_1_o));
  // CPU_ENABLE_8 cpu_enable_8_1: pin names not known; wires that end beside it: O, or_8_1_o, decoder_3x8_1_o[2]
  // CPU_ENABLE_8 cpu_enable_8_2: pin names not known; wires that end beside it: O, and_8_1_o, decoder_3x8_1_o[3]
  // CPU_ENABLE_8 cpu_enable_8_3: pin names not known; wires that end beside it: O, not_8_1_o, decoder_3x8_1_o[4]
  // CPU_ENABLE_8 cpu_enable_8_4: pin names not known; wires that end beside it: decoder_3x8_1_o[4], shl_1_o, decoder_3x8_1_o[5]
  and and_3 (Carry_Out, shl_1_shift_out, decoder_3x8_1_o[5]);
  // CPU_ENABLE_8 cpu_enable_8_5: pin names not known; wires that end beside it: O, shr_1_o, decoder_3x8_1_o[6]
  // CPU_ENABLE_8 cpu_enable_8_6: pin names not known; wires that end beside it: O, cpu_adder_8_1_o, decoder_3x8_1_o[1]
  // CPU_ENABLE_8 cpu_enable_8_7: pin names not known; wires that end beside it: O, xor_8_1_o, decoder_3x8_1_o[0]
  CPU_Z cpu_z_1 (.I(O), .O(zero));

  // Notes on the sheet:
  //   E
  //   E
  //   E
  //   E
  //   E
  //   E
  //   E
  //   Z
endmodule

module Decoder_3x8 (
  input  A,
  input  B,
  input  C,
  output [7:0] O
);

  wire not_1_out, not_2_out, not_3_out;

  not not_1 (not_1_out, A);
  not not_2 (not_2_out, B);
  not not_3 (not_3_out, C);
  and and_1 (O[0], not_1_out, not_2_out, not_3_out);
  and and_2 (O[1], not_1_out, not_2_out, C);
  and and_3 (O[2], not_1_out, B, not_3_out);
  and and_4 (O[3], not_1_out, B, C);
  and and_5 (O[4], A, not_2_out, not_3_out);
  and and_6 (O[5], A, not_2_out, C);
  and and_7 (O[6], A, B, not_3_out);
  and and_8 (O[7], A, B, C);
endmodule

module CPU_ADDER_8 (
  input  [7:0] A,
  input  carry_in,
  input  [7:0] B,
  output carry_out,
  output [7:0] O
);

  wire cpu_adder_2_carry_out, cpu_adder_3_carry_out, cpu_adder_4_carry_out, cpu_adder_5_carry_out,
       cpu_adder_6_carry_out, cpu_adder_7_carry_out, cpu_adder_8_carry_out;

  CPU_ADDER cpu_adder_1 (.a(A[0]), .b(B[0]), .carry_in(cpu_adder_2_carry_out), .carry_out(carry_out), .sum(O[0]));
  CPU_ADDER cpu_adder_2 (
    .a(A[1]), .b(B[1]), .carry_in(cpu_adder_3_carry_out), .carry_out(cpu_adder_2_carry_out), .sum(O[1]));
  CPU_ADDER cpu_adder_3 (
    .a(A[2]), .b(B[2]), .carry_in(cpu_adder_4_carry_out), .carry_out(cpu_adder_3_carry_out), .sum(O[2]));
  CPU_ADDER cpu_adder_4 (
    .a(A[3]), .b(B[3]), .carry_in(cpu_adder_5_carry_out), .carry_out(cpu_adder_4_carry_out), .sum(O[3]));
  CPU_ADDER cpu_adder_5 (
    .a(A[4]), .b(B[4]), .carry_in(cpu_adder_6_carry_out), .carry_out(cpu_adder_5_carry_out), .sum(O[4]));
  CPU_ADDER cpu_adder_6 (
    .a(A[5]), .b(B[5]), .carry_in(cpu_adder_7_carry_out), .carry_out(cpu_adder_6_carry_out), .sum(O[5]));
  CPU_ADDER cpu_adder_7 (
    .a(A[6]), .b(B[6]), .carry_in(cpu_adder_8_carry_out), .carry_out(cpu_adder_7_carry_out), .sum(O[6]));
  CPU_ADDER cpu_adder_8 (.a(A[7]), .b(B[7]), .carry_in(carry_in), .carry_out(cpu_adder_8_carry_out), .sum(O[7]));
endmodule

module CPU_REG (
  input  [7:0] I,
  input  E,
  input  S,
  output [7:0] R,
  output [7:0] O
);

  CPU_REG_8 cpu_reg_8_1 (.I(I), .E(E), .S(S), .R(R), .O(O));
endmodule

module TEMP (
  input  [7:0] I,
  input  S,
  output [7:0] out_3
);

  wire [7:0] buffer_1_out;

  assign buffer_1_out = I;  // Buffer buffer_1, 8 bits wide
  CPU_MEM_8 cpu_mem_8_1 (.I(buffer_1_out), .S(S), .O(out_3));
endmodule

module CPU_ACC (
  input  [7:0] Acc,
  input  E,
  input  S,
  output [7:0] R,
  output [7:0] O
);

  CPU_REG_8 cpu_reg_8_1 (.I(Acc), .E(E), .S(S), .R(R), .O(O));
endmodule

module CPU_IAR (
  input  [7:0] IAR,
  input  E,
  input  S,
  output [7:0] R,
  output [7:0] O
);

  CPU_REG_8 cpu_reg_8_1 (.I(IAR), .E(E), .S(S), .R(R), .O(O));
endmodule

module CPU_IR (
  input  [7:0] IR,
  input  S,
  output [7:0] out_3
);

  wire [7:0] buffer_1_out;

  assign buffer_1_out = IR;  // Buffer buffer_1, 8 bits wide
  CPU_MEM_8 cpu_mem_8_1 (.I(buffer_1_out), .S(S), .O(out_3));
endmodule

module CPU_CLK (
  input  in_1,
  output clk,
  output clks,
  output clke
);

  wire j_k_ff_1_qn, nand_1_out;

  J_K_Flip_Flop j_k_ff_1 (.J(1'b1), .K(in_1), .clk(1'b1), .Q(clk), .Qn(j_k_ff_1_qn));  // open: preset, reset
  nand nand_1 (nand_1_out, in_1, clk);
  nand nand_2 (clke, j_k_ff_1_qn, in_1);
  not not_1 (clks, nand_1_out);
endmodule

module CPU_Stepper (
  input  reset,
  input  clk,
  output stp_1,
  output stp_2,
  output stp_3,
  output stp_4,
  output stp_5,
  output stp_6,
  output stp_7
);

  wire cpu_mem_1_1_q, cpu_mem_1_2_q, cpu_mem_1_3_q, cpu_mem_1_4_q, cpu_mem_1_5_q, cpu_mem_1_6_q,
       cpu_mem_1_7_q, cpu_mem_1_8_q, cpu_mem_1_9_q, cpu_mem_1_10_q, cpu_mem_1_11_q, not_1_out, not_2_out,
       not_3_out, not_4_out, not_5_out, not_6_out, not_7_out, not_8_out, or_1_out, or_2_out;

  not not_1 (not_1_out, reset);
  not not_2 (not_2_out, clk);
  or or_1 (or_1_out, reset, clk);
  or or_2 (or_2_out, reset, not_2_out);
  or or_3 (stp_1, reset, not_3_out);
  not not_3 (not_3_out, cpu_mem_1_2_q);
  CPU_MEM_1 cpu_mem_1_1 (.s(not_1_out), .q(cpu_mem_1_1_q));  // open: e
  and and_1 (stp_2, cpu_mem_1_2_q, not_4_out);
  not not_4 (not_4_out, cpu_mem_1_4_q);
  CPU_MEM_1 cpu_mem_1_2 (.s(not_1_out), .q(cpu_mem_1_2_q));  // open: e
  CPU_MEM_1 cpu_mem_1_3 (.s(not_1_out), .q(cpu_mem_1_3_q));  // open: e
  and and_2 (stp_3, cpu_mem_1_4_q, not_5_out);
  CPU_MEM_1 cpu_mem_1_4 (.s(not_1_out), .q(cpu_mem_1_4_q));  // open: e
  not not_5 (not_5_out, cpu_mem_1_6_q);
  CPU_MEM_1 cpu_mem_1_5 (.s(cpu_mem_1_1_q), .q(cpu_mem_1_5_q));  // open: e
  and and_3 (stp_4, cpu_mem_1_6_q, not_6_out);
  not not_6 (not_6_out, cpu_mem_1_8_q);
  CPU_MEM_1 cpu_mem_1_6 (.s(cpu_mem_1_2_q), .e(or_1_out), .q(cpu_mem_1_6_q));
  CPU_MEM_1 cpu_mem_1_7 (.s(cpu_mem_1_3_q), .e(or_2_out), .q(cpu_mem_1_7_q));
  and and_4 (stp_5, cpu_mem_1_8_q, not_7_out);
  CPU_MEM_1 cpu_mem_1_8 (.s(cpu_mem_1_4_q), .e(or_1_out), .q(cpu_mem_1_8_q));
  not not_7 (not_7_out, cpu_mem_1_10_q);
  CPU_MEM_1 cpu_mem_1_9 (.s(cpu_mem_1_5_q), .e(or_2_out), .q(cpu_mem_1_9_q));
  and and_5 (stp_6, cpu_mem_1_10_q, not_8_out);
  not not_8 (not_8_out, stp_7);
  CPU_MEM_1 cpu_mem_1_10 (.s(cpu_mem_1_6_q), .q(cpu_mem_1_10_q));  // open: e
  CPU_MEM_1 cpu_mem_1_11 (.s(cpu_mem_1_7_q), .q(cpu_mem_1_11_q));  // open: e
  // CPU_MEM_1 cpu_mem_1_12: pin names not known; wires that end beside it: cpu_mem_1_8_q, or_1_out, cpu_mem_1_9_q, or_2_out, cpu_mem_1_10_q, or_1_out, cpu_mem_1_11_q, or_2_out, stp_7
endmodule

module CPU_CCU (
  input  clk,
  input  clks,
  input  clke,
  output MAR_S,
  output RAM_E,
  output RAM_S,
  output ACC_S,
  output ACC_E,
  output TMP_S,
  output R0_S,
  output R0_E,
  output R1_S,
  output R2_S,
  output R1_E,
  output R2_E,
  output R3_S,
  output R3_E
);

  wire buffer_1_out, cpu_stepper_1_stp_4, cpu_stepper_1_stp_5, cpu_stepper_1_stp_6, undriven;

  and and_1 (RAM_E, clke, 1'b0);
  and and_2 (ACC_E, clke, cpu_stepper_1_stp_6);
  and and_3 (R0_E, clke, cpu_stepper_1_stp_5);
  and and_4 (R1_E, clke, cpu_stepper_1_stp_4);
  and and_5 (R2_E, clke, 1'b0);
  and and_6 (R3_E, clke, 1'b0);
  buf buffer_1 (buffer_1_out, undriven);
  CPU_Stepper cpu_stepper_1 (
    .reset(undriven), .clk(clk), .stp_4(cpu_stepper_1_stp_4), .stp_5(cpu_stepper_1_stp_5),
    .stp_6(cpu_stepper_1_stp_6), .stp_7(buffer_1_out));  // open: stp_1, stp_2, stp_3
  and and_7 (MAR_S, clks, 1'b0);
  and and_8 (RAM_S, clks, cpu_stepper_1_stp_5);
  and and_9 (ACC_S, clks, 1'b0);
  and and_10 (TMP_S, clks, cpu_stepper_1_stp_4);
  and and_11 (R0_S, clks, 1'b0);
  and and_12 (R1_S, clks, 1'b0);
  and and_13 (R2_S, clks, 1'b0);
  and and_14 (R3_S, clks, cpu_stepper_1_stp_6);
endmodule

module CPU (
);

  TEMP temp_1 ();  // open: I, S, out_3
  CPU_ALU cpu_alu_1 ();  // open: A, carry_in, B, in_4, in_5, in_6, a_larger, equal, zero, O, Carry_Out
  CPU_ACC cpu_acc_1 ();  // open: Acc, E, S, R, O
  CPU_CLK cpu_clk_1 ();  // open: in_1, clk, clks, clke
  CPU_REG cpu_reg_1 ();  // open: I, E, S, R, O
  CPU_CCU cpu_ccu_1 ();  // open: clk, clks, clke, MAR_S, RAM_E, RAM_S, ACC_S, ACC_E, TMP_S, R0_S, R0_E, R1_S, R2_S, R1_E, R2_E, R3_S, R3_E
  CPU_REG cpu_reg_2 ();  // open: I, E, S, R, O
  RAM ram_1 ();  // open: addr, we, oe, clk, din, dout
  CPU_REG cpu_reg_3 ();  // open: I, E, S, R, O
  CPU_IAR cpu_iar_1 ();  // open: IAR, E, S, R, O
  CPU_IR cpu_ir_1 ();  // open: IR, S, out_3

  // Notes on the sheet:
  //   clk
endmodule
